// Logisim project Arithmetic_Circuits.circ as structural Verilog: 3 circuits, main circuit Half Adder
module Half_Adder (
  input  A,
  input  B,
  output Sum,
  output Cout
);

  xor xor_1 (Sum, A, B);
  and and_1 (Cout, B, A);
endmodule

module Full_Adder (
  input  Cin,
  input  A,
  input  B,
  output Sum,
  output Cout
);

  wire half_adder_1_cout, half_adder_1_sum, half_adder_2_cout;

  Half_Adder half_adder_1 (.A(A), .B(B), .Sum(half_adder_1_sum), .Cout(half_adder_1_cout));
  Half_Adder half_adder_2 (.A(Cin), .B(half_adder_1_sum), .Sum(Sum), .Cout(half_adder_2_cout));
  or or_1 (Cout, half_adder_2_cout, half_adder_1_cout);
endmodule

module _8_bit_Adder_Subtractor_v1_1 (
  input  [7:0] A,
  input  [7:0] B,
  input  Sub,
  output [7:0] Sum_Diff,
  output Cout
);

  wire full_adder_1_cout, full_adder_2_cout, full_adder_3_cout, full_adder_4_cout, full_adder_5_cout,
       full_adder_6_cout, full_adder_7_cout, xor_1_out, xor_2_out, xor_3_out, xor_4_out, xor_5_out,
       xor_6_out, xor_7_out, xor_8_out;

  xor xor_1 (xor_1_out, B[0], Sub);
  xor xor_2 (xor_2_out, B[1], Sub);
  xor xor_3 (xor_3_out, B[2], Sub);
  xor xor_4 (xor_4_out, B[3], Sub);
  xor xor_5 (xor_5_out, B[4], Sub);
  xor xor_6 (xor_6_out, B[5], Sub);
  xor xor_7 (xor_7_out, B[6], Sub);
  xor xor_8 (xor_8_out, B[7], Sub);
  Full_Adder full_adder_1 (.Cin(Sub), .A(A[0]), .B(xor_1_out), .Sum(Sum_Diff[0]), .Cout(full_adder_1_cout));
  Full_Adder full_adder_2 (
    .Cin(full_adder_1_cout), .A(A[1]), .B(xor_2_out), .Sum(Sum_Diff[1]), .Cout(full_adder_2_cout));
  Full_Adder full_adder_3 (
    .Cin(full_adder_2_cout), .A(A[2]), .B(xor_3_out), .Sum(Sum_Diff[2]), .Cout(full_adder_3_cout));
  Full_Adder full_adder_4 (
    .Cin(full_adder_3_cout), .A(A[3]), .B(xor_4_out), .Sum(Sum_Diff[3]), .Cout(full_adder_4_cout));
  Full_Adder full_adder_5 (
    .Cin(full_adder_4_cout), .A(A[4]), .B(xor_5_out), .Sum(Sum_Diff[4]), .Cout(full_adder_5_cout));
  Full_Adder full_adder_6 (
    .Cin(full_adder_5_cout), .A(A[5]), .B(xor_6_out), .Sum(Sum_Diff[5]), .Cout(full_adder_6_cout));
  Full_Adder full_adder_7 (
    .Cin(full_adder_6_cout), .A(A[6]), .B(xor_7_out), .Sum(Sum_Diff[6]), .Cout(full_adder_7_cout));
  Full_Adder full_adder_8 (.Cin(full_adder_7_cout), .A(A[7]), .B(xor_8_out), .Sum(Sum_Diff[7]), .Cout(Cout));
endmodule
