// Logisim project CPU_project.circ as structural Verilog: 2 circuits, main circuit I-Bit ALU
module I_Bit_ALU (
  input  Sub,
  input  Cin,
  input  [2:0] in_3,
  input  A,
  input  B,
  input  Less,
  output Result,
  output Cout,
  output Set
);

  wire and_1_out, nor_1_out, or_1_out, xor_1_out, xor_2_out;

  xor xor_1 (xor_1_out, B, Sub);
  and and_1 (and_1_out, A, B);
  or or_1 (or_1_out, A, B);
  xor xor_2 (xor_2_out, A, B);
  nor nor_1 (nor_1_out, A, B);
  Adder #(.width(1)) adder_1 (.a(A), .b(xor_1_out), .out(Set), .cin(Cin), .cout(Cout));
  Multiplexer #(.select(3), .enable("false")) multiplexer_1 (
    .in0(and_1_out), .in1(or_1_out), .in2(xor_2_out), .in3(nor_1_out), .in4(Set), .in5(Less), .out(Result),
    .sel(in_3));  // open: in6, in7
endmodule

module ALU (
  input  Sub,
  input  [2:0] Op,
  input  [7:0] A,
  input  [7:0] B,
  output [7:0] R,
  output Zero
);

  wire i_bit_alu_1_cout, i_bit_alu_2_cout, i_bit_alu_3_cout, i_bit_alu_4_cout, i_bit_alu_5_cout,
       i_bit_alu_6_cout, i_bit_alu_7_cout, i_bit_alu_8_set;

  I_Bit_ALU i_bit_alu_1 (
    .A(A[0]), .B(B[0]), .Less(i_bit_alu_8_set), .Result(R[0]), .Sub(Sub), .Cin(Sub), .in_3(Op),
    .Cout(i_bit_alu_1_cout));  // open: Set
  I_Bit_ALU i_bit_alu_2 (
    .A(A[1]), .B(B[1]), .Less(1'b0), .Result(R[1]), .Sub(Sub), .Cin(i_bit_alu_1_cout), .in_3(Op),
    .Cout(i_bit_alu_2_cout));  // open: Set
  I_Bit_ALU i_bit_alu_3 (
    .A(A[2]), .B(B[2]), .Less(1'b0), .Result(R[2]), .Sub(Sub), .Cin(i_bit_alu_2_cout), .in_3(Op),
    .Cout(i_bit_alu_3_cout));  // open: Set
  I_Bit_ALU i_bit_alu_4 (
    .A(A[3]), .B(B[3]), .Less(1'b0), .Result(R[3]), .Sub(Sub), .Cin(i_bit_alu_3_cout), .in_3(Op),
    .Cout(i_bit_alu_4_cout));  // open: Set
  I_Bit_ALU i_bit_alu_5 (
    .A(A[4]), .B(B[4]), .Less(1'b0), .Result(R[4]), .Sub(Sub), .Cin(i_bit_alu_4_cout), .in_3(Op),
    .Cout(i_bit_alu_5_cout));  // open: Set
  I_Bit_ALU i_bit_alu_6 (
    .A(A[5]), .B(B[5]), .Less(1'b0), .Result(R[5]), .Sub(Sub), .Cin(i_bit_alu_5_cout), .in_3(Op),
    .Cout(i_bit_alu_6_cout));  // open: Set
  I_Bit_ALU i_bit_alu_7 (
    .A(A[6]), .B(B[6]), .Less(1'b0), .Result(R[6]), .Sub(Sub), .Cin(i_bit_alu_6_cout), .in_3(Op),
    .Cout(i_bit_alu_7_cout));  // open: Set
  I_Bit_ALU i_bit_alu_8 (
    .A(A[7]), .B(B[7]), .Less(1'b0), .Result(R[7]), .Sub(Sub), .Cin(i_bit_alu_7_cout), .in_3(Op),
    .Set(i_bit_alu_8_set));  // open: Cout
  nor nor_1 (Zero, R[0], R[1], R[2], R[3], R[4], R[5], R[6], R[7]);
endmodule
