// Logisim project Memory.circ as structural Verilog
module _4x4_RAM_Array_v1_1 (
  input  in_1,
  input  in_2,
  input  in_3,
  input  in_4,
  input  [1:0] in_5,
  input  WE,
  output out_7,
  output out_8,
  output out_9,
  output out_10
);

  wire and_1_out, and_2_out, and_3_out, and_4_out, and_5_out, and_6_out, and_7_out, and_8_out, and_9_out,
       and_10_out, and_11_out, and_12_out, and_13_out, and_14_out, and_15_out, and_16_out, and_17_out,
       and_18_out, and_19_out, and_20_out, d_ff_1_q, d_ff_2_q, d_ff_3_q, d_ff_4_q, d_ff_5_q, d_ff_6_q,
       d_ff_7_q, d_ff_8_q, d_ff_9_q, d_ff_10_q, d_ff_11_q, d_ff_12_q, d_ff_13_q, d_ff_14_q, d_ff_15_q,
       d_ff_16_q, decoder_1_out0, decoder_1_out1, decoder_1_out2, decoder_1_out3, undriven, undriven_2,
       undriven_3, undriven_4, undriven_5, undriven_6, undriven_7, undriven_8, undriven_9, undriven_10,
       undriven_11, undriven_12, undriven_13, undriven_14, undriven_15, undriven_16;

  Decoder #(.select(2), .disabled(0), .enable("false")) decoder_1 (
    .out0(decoder_1_out0), .out1(decoder_1_out1), .out2(decoder_1_out2), .out3(decoder_1_out3), .sel(in_5));
  and and_1 (and_1_out, decoder_1_out0, WE);
  D_Flip_Flop #(.trigger("high")) d_ff_1 (
    .clk(and_1_out), .D(in_1), .Q(d_ff_1_q), .en(undriven), .reset(undriven));  // open: Qn, preset
  and and_2 (and_2_out, decoder_1_out1, WE);
  D_Flip_Flop #(.trigger("high")) d_ff_2 (
    .clk(and_2_out), .D(in_1), .Q(d_ff_2_q), .en(undriven_2), .reset(undriven_2));  // open: Qn, preset
  and and_3 (and_3_out, decoder_1_out2, WE);
  D_Flip_Flop #(.trigger("high")) d_ff_3 (
    .clk(and_3_out), .D(in_1), .Q(d_ff_3_q), .en(undriven_3), .reset(undriven_3));  // open: Qn, preset
  and and_4 (and_4_out, decoder_1_out3, WE);
  D_Flip_Flop #(.trigger("high")) d_ff_4 (
    .clk(and_4_out), .D(in_1), .Q(d_ff_4_q), .en(undriven_4), .reset(undriven_4));  // open: Qn, preset
  and and_5 (and_5_out, d_ff_1_q, decoder_1_out0);
  and and_6 (and_6_out, d_ff_2_q, decoder_1_out1);
  and and_7 (and_7_out, d_ff_3_q, decoder_1_out2);
  and and_8 (and_8_out, d_ff_4_q, decoder_1_out3);
  or or_1 (out_7, and_8_out, and_7_out, and_6_out, and_5_out);
  D_Flip_Flop #(.trigger("high")) d_ff_5 (
    .clk(and_1_out), .D(in_2), .Q(d_ff_5_q), .en(undriven_5), .reset(undriven_5));  // open: Qn, preset
  D_Flip_Flop #(.trigger("high")) d_ff_6 (
    .clk(and_2_out), .D(in_2), .Q(d_ff_6_q), .en(undriven_6), .reset(undriven_6));  // open: Qn, preset
  D_Flip_Flop #(.trigger("high")) d_ff_7 (
    .clk(and_3_out), .D(in_2), .Q(d_ff_7_q), .en(undriven_7), .reset(undriven_7));  // open: Qn, preset
  D_Flip_Flop #(.trigger("high")) d_ff_8 (
    .clk(and_4_out), .D(in_2), .Q(d_ff_8_q), .en(undriven_8), .reset(undriven_8));  // open: Qn, preset
  and and_9 (and_9_out, d_ff_5_q, decoder_1_out0);
  and and_10 (and_10_out, d_ff_6_q, decoder_1_out1);
  and and_11 (and_11_out, d_ff_7_q, decoder_1_out2);
  and and_12 (and_12_out, d_ff_8_q, decoder_1_out3);
  or or_2 (out_8, and_12_out, and_11_out, and_10_out, and_9_out);
  D_Flip_Flop #(.trigger("high")) d_ff_9 (
    .clk(and_1_out), .D(in_3), .Q(d_ff_9_q), .en(undriven_9), .reset(undriven_9));  // open: Qn, preset
  D_Flip_Flop #(.trigger("high")) d_ff_10 (
    .clk(and_2_out), .D(in_3), .Q(d_ff_10_q), .en(undriven_10), .reset(undriven_10));  // open: Qn, preset
  D_Flip_Flop #(.trigger("high")) d_ff_11 (
    .clk(and_3_out), .D(in_3), .Q(d_ff_11_q), .en(undriven_11), .reset(undriven_11));  // open: Qn, preset
  D_Flip_Flop #(.trigger("high")) d_ff_12 (
    .clk(and_4_out), .D(in_3), .Q(d_ff_12_q), .en(undriven_12), .reset(undriven_12));  // open: Qn, preset
  and and_13 (and_13_out, d_ff_9_q, decoder_1_out0);
  and and_14 (and_14_out, d_ff_10_q, decoder_1_out1);
  and and_15 (and_15_out, d_ff_11_q, decoder_1_out2);
  and and_16 (and_16_out, d_ff_12_q, decoder_1_out3);
  or or_3 (out_9, and_16_out, and_15_out, and_14_out, and_13_out);
  D_Flip_Flop #(.trigger("high")) d_ff_13 (
    .clk(and_1_out), .D(in_4), .Q(d_ff_13_q), .en(undriven_13), .reset(undriven_13));  // open: Qn, preset
  and and_17 (and_17_out, d_ff_13_q, decoder_1_out0);
  D_Flip_Flop #(.trigger("high")) d_ff_14 (
    .clk(and_2_out), .D(in_4), .Q(d_ff_14_q), .en(undriven_14), .reset(undriven_14));  // open: Qn, preset
  and and_18 (and_18_out, d_ff_14_q, decoder_1_out1);
  D_Flip_Flop #(.trigger("high")) d_ff_15 (
    .clk(and_3_out), .D(in_4), .Q(d_ff_15_q), .en(undriven_15), .reset(undriven_15));  // open: Qn, preset
  and and_19 (and_19_out, d_ff_15_q, decoder_1_out2);
  D_Flip_Flop #(.trigger("high")) d_ff_16 (
    .clk(and_4_out), .D(in_4), .Q(d_ff_16_q), .en(undriven_16), .reset(undriven_16));  // open: Qn, preset
  and and_20 (and_20_out, d_ff_16_q, decoder_1_out3);
  or or_4 (out_10, and_20_out, and_19_out, and_18_out, and_17_out);
endmodule

module _4x4_RAM_Array_v1_2 (
  input  in_1,
  input  in_2,
  input  in_3,
  input  in_4,
  input  WE,
  input  [1:0] in_6,
  output out_7,
  output out_8,
  output out_9,
  output out_10
);

  wire and_1_out, and_2_out, and_3_out, and_4_out, d_ff_1_q, d_ff_2_q, d_ff_3_q, d_ff_4_q, d_ff_5_q,
       d_ff_6_q, d_ff_7_q, d_ff_8_q, d_ff_9_q, d_ff_10_q, d_ff_11_q, d_ff_12_q, d_ff_13_q, d_ff_14_q,
       d_ff_15_q, d_ff_16_q, decoder_1_out0, decoder_1_out1, decoder_1_out2, decoder_1_out3, undriven,
       undriven_2, undriven_3, undriven_4, undriven_5, undriven_6, undriven_7, undriven_8, undriven_9,
       undriven_10, undriven_11, undriven_12, undriven_13, undriven_14, undriven_15, undriven_16;

  Decoder #(.select(2), .disabled(0), .enable("false")) decoder_1 (
    .out0(decoder_1_out0), .out1(decoder_1_out1), .out2(decoder_1_out2), .out3(decoder_1_out3), .sel(in_6));
  and and_1 (and_1_out, decoder_1_out0, WE);
  D_Flip_Flop #(.trigger("high")) d_ff_1 (
    .clk(and_1_out), .D(in_1), .Q(d_ff_1_q), .en(undriven), .reset(undriven));  // open: Qn, preset
  and and_2 (and_2_out, decoder_1_out1, WE);
  D_Flip_Flop #(.trigger("high")) d_ff_2 (
    .clk(and_2_out), .D(in_1), .Q(d_ff_2_q), .en(undriven_2), .reset(undriven_2));  // open: Qn, preset
  and and_3 (and_3_out, decoder_1_out2, WE);
  D_Flip_Flop #(.trigger("high")) d_ff_3 (
    .clk(and_3_out), .D(in_1), .Q(d_ff_3_q), .en(undriven_3), .reset(undriven_3));  // open: Qn, preset
  and and_4 (and_4_out, decoder_1_out3, WE);
  D_Flip_Flop #(.trigger("high")) d_ff_4 (
    .clk(and_4_out), .D(in_1), .Q(d_ff_4_q), .en(undriven_4), .reset(undriven_4));  // open: Qn, preset
  D_Flip_Flop #(.trigger("high")) d_ff_5 (
    .clk(and_1_out), .D(in_2), .Q(d_ff_5_q), .en(undriven_5), .reset(undriven_5));  // open: Qn, preset
  D_Flip_Flop #(.trigger("high")) d_ff_6 (
    .clk(and_2_out), .D(in_2), .Q(d_ff_6_q), .en(undriven_6), .reset(undriven_6));  // open: Qn, preset
  D_Flip_Flop #(.trigger("high")) d_ff_7 (
    .clk(and_3_out), .D(in_2), .Q(d_ff_7_q), .en(undriven_7), .reset(undriven_7));  // open: Qn, preset
  D_Flip_Flop #(.trigger("high")) d_ff_8 (
    .clk(and_4_out), .D(in_2), .Q(d_ff_8_q), .en(undriven_8), .reset(undriven_8));  // open: Qn, preset
  Multiplexer #(.select(2), .disabled(0), .enable("false")) multiplexer_1 (
    .in0(d_ff_1_q), .in1(d_ff_2_q), .in2(d_ff_3_q), .in3(d_ff_4_q), .out(out_7), .sel(in_6));
  Multiplexer #(.select(2), .disabled(0), .enable("false")) multiplexer_2 (
    .in0(d_ff_5_q), .in1(d_ff_6_q), .in2(d_ff_7_q), .in3(d_ff_8_q), .out(out_8), .sel(in_6));
  D_Flip_Flop #(.trigger("high")) d_ff_9 (
    .clk(and_1_out), .D(in_3), .Q(d_ff_9_q), .en(undriven_9), .reset(undriven_9));  // open: Qn, preset
  D_Flip_Flop #(.trigger("high")) d_ff_10 (
    .clk(and_2_out), .D(in_3), .Q(d_ff_10_q), .en(undriven_10), .reset(undriven_10));  // open: Qn, preset
  D_Flip_Flop #(.trigger("high")) d_ff_11 (
    .clk(and_3_out), .D(in_3), .Q(d_ff_11_q), .en(undriven_11), .reset(undriven_11));  // open: Qn, preset
  D_Flip_Flop #(.trigger("high")) d_ff_12 (
    .clk(and_4_out), .D(in_3), .Q(d_ff_12_q), .en(undriven_12), .reset(undriven_12));  // open: Qn, preset
  D_Flip_Flop #(.trigger("high")) d_ff_13 (
    .clk(and_1_out), .D(in_4), .Q(d_ff_13_q), .en(undriven_13), .reset(undriven_13));  // open: Qn, preset
  D_Flip_Flop #(.trigger("high")) d_ff_14 (
    .clk(and_2_out), .D(in_4), .Q(d_ff_14_q), .en(undriven_14), .reset(undriven_14));  // open: Qn, preset
  D_Flip_Flop #(.trigger("high")) d_ff_15 (
    .clk(and_3_out), .D(in_4), .Q(d_ff_15_q), .en(undriven_15), .reset(undriven_15));  // open: Qn, preset
  D_Flip_Flop #(.trigger("high")) d_ff_16 (
    .clk(and_4_out), .D(in_4), .Q(d_ff_16_q), .en(undriven_16), .reset(undriven_16));  // open: Qn, preset
  Multiplexer #(.select(2), .disabled(0), .enable("false")) multiplexer_3 (
    .in0(d_ff_9_q), .in1(d_ff_10_q), .in2(d_ff_11_q), .in3(d_ff_12_q), .out(out_9), .sel(in_6));
  Multiplexer #(.select(2), .disabled(0), .enable("false")) multiplexer_4 (
    .in0(d_ff_13_q), .in1(d_ff_14_q), .in2(d_ff_15_q), .in3(d_ff_16_q), .out(out_10), .sel(in_6));
endmodule
