// Logisim project Transistors_to_Gates.circ as structural Verilog
module NAND_Gate (
  input  A,
  input  B,
  output F
);

  wire transistor_3_out, transistor_4_out;

  Transistor transistor_1 (.in(1'b1), .out(F), .gate(A));
  Transistor transistor_2 (.in(1'b1), .out(F), .gate(B));
  Transistor #(.\type ("n")) transistor_3 (.in(F), .out(transistor_3_out), .gate(A));
  Transistor #(.\type ("n")) transistor_4 (.in(transistor_3_out), .out(transistor_4_out), .gate(B));
  // also tied to GND on the sheet: transistor_4_out
endmodule

module NOR_Gate (
  input  A,
  input  B,
  output F
);

  wire transistor_1_out, transistor_3_out;

  Transistor transistor_1 (.in(1'b1), .out(transistor_1_out), .gate(A));
  Transistor transistor_2 (.in(transistor_1_out), .out(F), .gate(B));
  Transistor #(.\type ("n")) transistor_3 (.in(F), .out(transistor_3_out), .gate(B));
  Transistor #(.\type ("n")) transistor_4 (.in(F), .out(transistor_3_out), .gate(A));
  // also tied to GND on the sheet: transistor_3_out
endmodule

module NOT_Gate (
  input  A,
  output F
);

  wire transistor_2_out;

  Transistor transistor_1 (.in(1'b1), .out(F), .gate(A));
  Transistor #(.\type ("n")) transistor_2 (.in(F), .out(transistor_2_out), .gate(A));
  // also tied to GND on the sheet: transistor_2_out
endmodule
