// Logisim project alu.circ as structural Verilog: 3 circuits, main circuit I-Bit ALU
module I_Bit_ALU (
  input  Sub,
  input  Cin,
  input  [2:0] in_3,
  input  A,
  input  B,
  input  Less,
  output Result,
  output Cout,
  output Set
);

  wire and_1_out, nor_1_out, or_1_out, xor_1_out, xor_2_out;

  xor xor_1 (xor_1_out, B, Sub);
  and and_1 (and_1_out, A, B);
  or or_1 (or_1_out, A, B);
  xor xor_2 (xor_2_out, A, B);
  nor nor_1 (nor_1_out, A, B);
  Adder #(.width(1)) adder_1 (.a(A), .b(xor_1_out), .out(Set), .cin(Cin), .cout(Cout));
  Multiplexer #(.select(3), .enable("false")) multiplexer_1 (
    .in0(and_1_out), .in1(or_1_out), .in2(xor_2_out), .in3(nor_1_out), .in4(Set), .in5(Less), .out(Result),
    .sel(in_3));  // open: in6, in7

  // Notes on the sheet:
  //   000 => AND
  //   001 => OR
  //   010 => XOR
  //   011 => NOR
  //   100 => ADD/SUB
  //   101 => SLT
endmodule

module _8_bit_ALU (
  input  Sub,
  input  [2:0] Op,
  input  [7:0] A,
  input  [7:0] B,
  output [7:0] R,
  output Zero
);

  wire i_bit_alu_1_cout, i_bit_alu_2_cout, i_bit_alu_3_cout, i_bit_alu_4_cout, i_bit_alu_5_cout,
       i_bit_alu_6_cout, i_bit_alu_7_cout, i_bit_alu_8_set;

  I_Bit_ALU i_bit_alu_1 (
    .A(A[0]), .B(B[0]), .Less(i_bit_alu_8_set), .Result(R[0]), .Sub(Sub), .Cin(Sub), .in_3(Op),
    .Cout(i_bit_alu_1_cout));  // open: Set
  I_Bit_ALU i_bit_alu_2 (
    .A(A[1]), .B(B[1]), .Less(1'b0), .Result(R[1]), .Sub(Sub), .Cin(i_bit_alu_1_cout), .in_3(Op),
    .Cout(i_bit_alu_2_cout));  // open: Set
  I_Bit_ALU i_bit_alu_3 (
    .A(A[2]), .B(B[2]), .Less(1'b0), .Result(R[2]), .Sub(Sub), .Cin(i_bit_alu_2_cout), .in_3(Op),
    .Cout(i_bit_alu_3_cout));  // open: Set
  I_Bit_ALU i_bit_alu_4 (
    .A(A[3]), .B(B[3]), .Less(1'b0), .Result(R[3]), .Sub(Sub), .Cin(i_bit_alu_3_cout), .in_3(Op),
    .Cout(i_bit_alu_4_cout));  // open: Set
  I_Bit_ALU i_bit_alu_5 (
    .A(A[4]), .B(B[4]), .Less(1'b0), .Result(R[4]), .Sub(Sub), .Cin(i_bit_alu_4_cout), .in_3(Op),
    .Cout(i_bit_alu_5_cout));  // open: Set
  I_Bit_ALU i_bit_alu_6 (
    .A(A[5]), .B(B[5]), .Less(1'b0), .Result(R[5]), .Sub(Sub), .Cin(i_bit_alu_5_cout), .in_3(Op),
    .Cout(i_bit_alu_6_cout));  // open: Set
  I_Bit_ALU i_bit_alu_7 (
    .A(A[6]), .B(B[6]), .Less(1'b0), .Result(R[6]), .Sub(Sub), .Cin(i_bit_alu_6_cout), .in_3(Op),
    .Cout(i_bit_alu_7_cout));  // open: Set
  I_Bit_ALU i_bit_alu_8 (
    .A(A[7]), .B(B[7]), .Less(1'b0), .Result(R[7]), .Sub(Sub), .Cin(i_bit_alu_7_cout), .in_3(Op),
    .Set(i_bit_alu_8_set));  // open: Cout
  nor nor_1 (Zero, R[0], R[1], R[2], R[3], R[4], R[5], R[6], R[7]);
endmodule

module _32_bit_ALU (
  input  sub,
  input  [2:0] op,
  input  [31:0] a,
  input  [31:0] b,
  output [31:0] result,
  output Zero_Flag
);

  wire i_bit_alu_1_cout, i_bit_alu_2_cout, i_bit_alu_3_cout, i_bit_alu_4_cout, i_bit_alu_5_cout,
       i_bit_alu_6_cout, i_bit_alu_7_cout, i_bit_alu_8_cout, i_bit_alu_9_cout, i_bit_alu_10_cout,
       i_bit_alu_11_cout, i_bit_alu_12_cout, i_bit_alu_13_cout, i_bit_alu_14_cout, i_bit_alu_15_cout,
       i_bit_alu_16_cout, i_bit_alu_17_cout, i_bit_alu_18_cout, i_bit_alu_19_cout, i_bit_alu_20_cout,
       i_bit_alu_21_cout, i_bit_alu_22_cout, i_bit_alu_23_cout, i_bit_alu_24_cout, i_bit_alu_25_cout,
       i_bit_alu_26_cout, i_bit_alu_27_cout, i_bit_alu_28_cout, i_bit_alu_29_cout, i_bit_alu_30_cout,
       i_bit_alu_31_cout, i_bit_alu_32_set;

  I_Bit_ALU i_bit_alu_1 (
    .A(a[0]), .B(b[0]), .Less(i_bit_alu_32_set), .Result(result[0]), .Sub(sub), .Cin(sub), .in_3(op),
    .Cout(i_bit_alu_1_cout));  // open: Set
  I_Bit_ALU i_bit_alu_2 (
    .A(a[1]), .B(b[1]), .Less(1'b0), .Result(result[1]), .Sub(sub), .Cin(i_bit_alu_1_cout), .in_3(op),
    .Cout(i_bit_alu_2_cout));  // open: Set
  I_Bit_ALU i_bit_alu_3 (
    .A(a[2]), .B(b[2]), .Less(1'b0), .Result(result[2]), .Sub(sub), .Cin(i_bit_alu_2_cout), .in_3(op),
    .Cout(i_bit_alu_3_cout));  // open: Set
  I_Bit_ALU i_bit_alu_4 (
    .A(a[3]), .B(b[3]), .Less(1'b0), .Result(result[3]), .Sub(sub), .Cin(i_bit_alu_3_cout), .in_3(op),
    .Cout(i_bit_alu_4_cout));  // open: Set
  I_Bit_ALU i_bit_alu_5 (
    .A(a[4]), .B(b[4]), .Less(1'b0), .Result(result[4]), .Sub(sub), .Cin(i_bit_alu_4_cout), .in_3(op),
    .Cout(i_bit_alu_5_cout));  // open: Set
  I_Bit_ALU i_bit_alu_6 (
    .A(a[5]), .B(b[5]), .Less(1'b0), .Result(result[5]), .Sub(sub), .Cin(i_bit_alu_5_cout), .in_3(op),
    .Cout(i_bit_alu_6_cout));  // open: Set
  I_Bit_ALU i_bit_alu_7 (
    .A(a[6]), .B(b[6]), .Less(1'b0), .Result(result[6]), .Sub(sub), .Cin(i_bit_alu_6_cout), .in_3(op),
    .Cout(i_bit_alu_7_cout));  // open: Set
  I_Bit_ALU i_bit_alu_8 (
    .A(a[7]), .B(b[7]), .Less(1'b0), .Result(result[7]), .Sub(sub), .Cin(i_bit_alu_7_cout), .in_3(op),
    .Cout(i_bit_alu_8_cout));  // open: Set
  I_Bit_ALU i_bit_alu_9 (
    .A(a[8]), .B(b[8]), .Less(1'b0), .Result(result[8]), .Sub(sub), .Cin(i_bit_alu_8_cout), .in_3(op),
    .Cout(i_bit_alu_9_cout));  // open: Set
  I_Bit_ALU i_bit_alu_10 (
    .A(a[9]), .B(b[9]), .Less(1'b0), .Result(result[9]), .Sub(sub), .Cin(i_bit_alu_9_cout), .in_3(op),
    .Cout(i_bit_alu_10_cout));  // open: Set
  I_Bit_ALU i_bit_alu_11 (
    .A(a[10]), .B(b[10]), .Less(1'b0), .Result(result[10]), .Sub(sub), .Cin(i_bit_alu_10_cout), .in_3(op),
    .Cout(i_bit_alu_11_cout));  // open: Set
  I_Bit_ALU i_bit_alu_12 (
    .A(a[11]), .B(b[11]), .Less(1'b0), .Result(result[11]), .Sub(sub), .Cin(i_bit_alu_11_cout), .in_3(op),
    .Cout(i_bit_alu_12_cout));  // open: Set
  I_Bit_ALU i_bit_alu_13 (
    .A(a[12]), .B(b[12]), .Less(1'b0), .Result(result[12]), .Sub(sub), .Cin(i_bit_alu_12_cout), .in_3(op),
    .Cout(i_bit_alu_13_cout));  // open: Set
  I_Bit_ALU i_bit_alu_14 (
    .A(a[13]), .B(b[13]), .Less(1'b0), .Result(result[13]), .Sub(sub), .Cin(i_bit_alu_13_cout), .in_3(op),
    .Cout(i_bit_alu_14_cout));  // open: Set
  I_Bit_ALU i_bit_alu_15 (
    .A(a[14]), .B(b[14]), .Less(1'b0), .Result(result[14]), .Sub(sub), .Cin(i_bit_alu_14_cout), .in_3(op),
    .Cout(i_bit_alu_15_cout));  // open: Set
  I_Bit_ALU i_bit_alu_16 (
    .A(a[15]), .B(b[15]), .Less(1'b0), .Result(result[15]), .Sub(sub), .Cin(i_bit_alu_15_cout), .in_3(op),
    .Cout(i_bit_alu_16_cout));  // open: Set
  I_Bit_ALU i_bit_alu_17 (
    .A(a[16]), .B(b[16]), .Less(1'b0), .Result(result[16]), .Sub(sub), .Cin(i_bit_alu_16_cout), .in_3(op),
    .Cout(i_bit_alu_17_cout));  // open: Set
  I_Bit_ALU i_bit_alu_18 (
    .A(a[17]), .B(b[17]), .Less(1'b0), .Result(result[17]), .Sub(sub), .Cin(i_bit_alu_17_cout), .in_3(op),
    .Cout(i_bit_alu_18_cout));  // open: Set
  I_Bit_ALU i_bit_alu_19 (
    .A(a[18]), .B(b[18]), .Less(1'b0), .Result(result[18]), .Sub(sub), .Cin(i_bit_alu_18_cout), .in_3(op),
    .Cout(i_bit_alu_19_cout));  // open: Set
  I_Bit_ALU i_bit_alu_20 (
    .A(a[19]), .B(b[19]), .Less(1'b0), .Result(result[19]), .Sub(sub), .Cin(i_bit_alu_19_cout), .in_3(op),
    .Cout(i_bit_alu_20_cout));  // open: Set
  I_Bit_ALU i_bit_alu_21 (
    .A(a[20]), .B(b[20]), .Less(1'b0), .Result(result[20]), .Sub(sub), .Cin(i_bit_alu_20_cout), .in_3(op),
    .Cout(i_bit_alu_21_cout));  // open: Set
  I_Bit_ALU i_bit_alu_22 (
    .A(a[21]), .B(b[21]), .Less(1'b0), .Result(result[21]), .Sub(sub), .Cin(i_bit_alu_21_cout), .in_3(op),
    .Cout(i_bit_alu_22_cout));  // open: Set
  I_Bit_ALU i_bit_alu_23 (
    .A(a[22]), .B(b[22]), .Less(1'b0), .Result(result[22]), .Sub(sub), .Cin(i_bit_alu_22_cout), .in_3(op),
    .Cout(i_bit_alu_23_cout));  // open: Set
  I_Bit_ALU i_bit_alu_24 (
    .A(a[23]), .B(b[23]), .Less(1'b0), .Result(result[23]), .Sub(sub), .Cin(i_bit_alu_23_cout), .in_3(op),
    .Cout(i_bit_alu_24_cout));  // open: Set
  I_Bit_ALU i_bit_alu_25 (
    .A(a[24]), .B(b[24]), .Less(1'b0), .Result(result[24]), .Sub(sub), .Cin(i_bit_alu_24_cout), .in_3(op),
    .Cout(i_bit_alu_25_cout));  // open: Set
  I_Bit_ALU i_bit_alu_26 (
    .A(a[25]), .B(b[25]), .Less(1'b0), .Result(result[25]), .Sub(sub), .Cin(i_bit_alu_25_cout), .in_3(op),
    .Cout(i_bit_alu_26_cout));  // open: Set
  I_Bit_ALU i_bit_alu_27 (
    .A(a[26]), .B(b[26]), .Less(1'b0), .Result(result[26]), .Sub(sub), .Cin(i_bit_alu_26_cout), .in_3(op),
    .Cout(i_bit_alu_27_cout));  // open: Set
  I_Bit_ALU i_bit_alu_28 (
    .A(a[27]), .B(b[27]), .Less(1'b0), .Result(result[27]), .Sub(sub), .Cin(i_bit_alu_27_cout), .in_3(op),
    .Cout(i_bit_alu_28_cout));  // open: Set
  I_Bit_ALU i_bit_alu_29 (
    .A(a[28]), .B(b[28]), .Less(1'b0), .Result(result[28]), .Sub(sub), .Cin(i_bit_alu_28_cout), .in_3(op),
    .Cout(i_bit_alu_29_cout));  // open: Set
  I_Bit_ALU i_bit_alu_30 (
    .A(a[29]), .B(b[29]), .Less(1'b0), .Result(result[29]), .Sub(sub), .Cin(i_bit_alu_29_cout), .in_3(op),
    .Cout(i_bit_alu_30_cout));  // open: Set
  I_Bit_ALU i_bit_alu_31 (
    .A(a[30]), .B(b[30]), .Less(1'b0), .Result(result[30]), .Sub(sub), .Cin(i_bit_alu_30_cout), .in_3(op),
    .Cout(i_bit_alu_31_cout));  // open: Set
  I_Bit_ALU i_bit_alu_32 (
    .A(a[31]), .B(b[31]), .Less(1'b0), .Result(result[31]), .Sub(sub), .Cin(i_bit_alu_31_cout), .in_3(op),
    .Set(i_bit_alu_32_set));  // open: Cout
  nor nor_1 (Zero_Flag, result[0], result[1], result[2], result[3], result[4], result[5], result[6], result[7], result[8], result[9], result[10], result[11], result[12], result[13], result[14], result[15], result[16], result[17], result[18], result[19], result[20], result[21], result[22], result[23], result[24], result[25], result[26], result[27], result[28], result[29], result[30], result[31]);

  // Other names for the same wires on the sheet: q0 = result[0]; q1 = result[1]; q2 = result[2]; q3 = result[3];
  //   q4 = result[4]; q5 = result[5]; q6 = result[6]; q7 = result[7]; q8 = result[8]; q9 = result[9];
  //   q10 = result[10]; q11 = result[11]; q12 = result[12]; q13 = result[13]; q14 = result[14]; q15 = result[15];
  //   q16 = result[16]; q17 = result[17]; q18 = result[18]; q19 = result[19]; q20 = result[20]; q21 = result[21];
  //   q22 = result[22]; q23 = result[23]; q24 = result[24]; q25 = result[25]; q26 = result[26]; q27 = result[27];
  //   q28 = result[28]; q29 = result[29]; q30 = result[30]; q31 = result[31]
endmodule
