// Logisim project datapath.circ as structural Verilog: 4 circuits, main circuit main
module main (
  input  AlUop,
  input  [31:0] wdata,
  input  regDest,
  input  mem2reg,
  input  aluSrc,
  input  Store,
  input  in_7,
  output out_8
);

  wire clr, cu_1_p2, cu_1_p3, not_1_out;
  wire [2:0] alu_cu_1_out_3;
  wire [4:0] multiplexer_1_out;
  wire [23:0] adder_1_out, bit_extender_2_out, register_1_q;
  wire [31:0] bit_extender_1_out, main_1_out_8, main_1_out_9, multiplexer_2_out, multiplexer_3_out,
       n32_bit_alu_1_result, ram_1_data, ram_2_data;

  Register #(.width(24)) register_1 (.D(adder_1_out), .Q(register_1_q), .clk(in_7), .clr(clr));  // open: en
  Button button_1 (.out(clr));
  Adder #(.width(24)) adder_1 (.a(24'h1), .b(register_1_q), .out(adder_1_out));  // open: cin, cout
  not not_1 (not_1_out, Store);
  RAM #(.addrWidth(24), .dataWidth(32), .bus("separate")) ram_1 (
    .addr(register_1_q), .din(wdata), .data(ram_1_data), .str(Store), .clk(in_7), .ld(not_1_out), .clr(clr));  // open: sel
  Multiplexer #(.width(5), .enable("false")) multiplexer_1 (
    .in0(ram_1_data[20:16]), .in1(ram_1_data[15:11]), .out(multiplexer_1_out), .sel(regDest));
  // CU cu_1: pin names not known; wires that end beside it: ram_1_data[31:26], cu_1_p2, cu_1_p3, cu_1_p2
  assign bit_extender_1_out = {{16{ram_1_data[15]}}, ram_1_data[15:0]};  // Bit_Extender bit_extender_1
  register_file_main main_1 (
    .in_7(multiplexer_3_out), .out_8(main_1_out_8), .in_1(cu_1_p3), .in_3(clr), .in_6(multiplexer_1_out),
    .in_4(ram_1_data[25:21]), .in_5(ram_1_data[20:16]), .out_9(main_1_out_9), .in_2(in_7));
  Multiplexer #(.width(32), .enable("false")) multiplexer_2 (
    .in0(main_1_out_9), .in1(bit_extender_1_out), .out(multiplexer_2_out), .sel(aluSrc));
  _32_bit_ALU u_32_bit_alu_1 (
    .a(multiplexer_2_out), .b(main_1_out_8), .result(n32_bit_alu_1_result), .Zero_Flag(out_8),
    .op(alu_cu_1_out_3));  // open: sub
  ALU_CU alu_cu_1 (.in_1(ram_1_data[5:0]), .out_3(alu_cu_1_out_3), .in_2(AlUop));
  Bit_Extender #(.in_width(32), .out_width(24), .\type ("sign")) bit_extender_2 (
    .in(n32_bit_alu_1_result), .out(bit_extender_2_out));
  RAM #(.addrWidth(24), .dataWidth(32), .bus("separate")) ram_2 (
    .addr(bit_extender_2_out), .data(ram_2_data), .clk(in_7));  // open: din, str, sel, ld, clr
  Multiplexer #(.width(32), .enable("false")) multiplexer_3 (
    .in0(n32_bit_alu_1_result), .in1(ram_2_data), .out(multiplexer_3_out), .sel(mem2reg));

  // Other names for the same wires on the sheet: clk = in_7
endmodule

module ram_1 (
  input  [31:0] Store_data,
  input  [7:0] Address,
  input  Store,
  output [31:0] Data
);

  wire clock_1_out, not_1_out;

  assign Data = Store ? Store_data : 32'bz;  // Controlled_Buffer controlled_buffer_1
  not not_1 (not_1_out, Store);
  Clock clock_1 (.out(clock_1_out));
  RAM #(.dataWidth(32)) ram_1 (.addr(Address), .data(Data), .clk(clock_1_out), .ld(not_1_out));  // open: sel, clr
endmodule

module CU (
  input  [5:0] in_1,
  output out_2,
  output out_3,
  output [5:0] out_4
);

  assign {out_4[5:1], out_2} = in_1;  // Buffer buffer_1, 6 bits wide

  assign out_3 = out_2;
  assign out_4[0] = out_2;
endmodule

module ALU_CU (
  input  [5:0] in_1,
  input  in_2,
  output [2:0] out_3
);

  wire [5:3] buffer_1_out;

  assign {buffer_1_out, out_3} = in_1;  // Buffer buffer_1, 6 bits wide

  assign in_2 = in_1[2];
endmodule
