// Logisim project register_file.circ as structural Verilog: 1 circuit, main circuit main
module main (
  input  in_1,
  input  in_2,
  input  in_3,
  input  [4:0] in_4,
  input  [4:0] in_5,
  input  [4:0] in_6,
  input  [31:0] in_7,
  output [31:0] out_8,
  output [31:0] out_9
);

  wire and_1_out, and_2_out, and_3_out, and_4_out, and_5_out, and_6_out, and_7_out, and_8_out, and_9_out,
       and_10_out, and_11_out, and_12_out, and_13_out, and_14_out, and_15_out, and_16_out, and_17_out,
       and_18_out, and_19_out, and_20_out, and_21_out, and_22_out, and_23_out, and_24_out, and_25_out,
       and_26_out, and_27_out, and_28_out, and_29_out, and_30_out, and_31_out, and_32_out, r0c, r1c, r2c,
       r3c, r4c, r5c, r6c, r7c, r8c, r9c, r10c, r11c, r12c, r13c, r14c, r15c, r16c, r17c, r18c, r19c, r20c,
       r21c, r22c, r23c, r24c, r25c, r26c, r27c, r28c, r29c, r30c, r31c;
  wire [31:0] r0_in, r0_out, r1_in, r1_out, r2_in, r2_out, r3_in, r3_out, r4_in, r4_out, r5_in, r5_out,
       r6_in, r6_out, r7_in, r7_out, r8_in, r8_out, r9_in, r9_out, r10_in, r10_out, r11_in, r11_out, r12_in,
       r12_out, r13_in, r13_out, r14_in, r14_out, r15_in, r15_out, r16_in, r16_out, r17_in, r17_out, r18_in,
       r18_out, r19_in, r19_out, r20_in, r20_out, r21_in, r21_out, r22_in, r22_out, r23_in, r23_out, r24_in,
       r24_out, r25_in, r25_out, r26_in, r26_out, r27_in, r27_out, r28_in, r28_out, r29_in, r29_out, r30_in,
       r30_out, r31_in, r31_out;

  Demultiplexer #(.select(5), .width(32), .enable("false")) demultiplexer_1 (
    .out0(r0_in), .out1(r1_in), .out2(r2_in), .out3(r3_in), .out4(r4_in), .out5(r5_in), .out6(r6_in),
    .out7(r7_in), .out8(r8_in), .out9(r9_in), .out10(r10_in), .out11(r11_in), .out12(r12_in), .out13(r13_in),
    .out14(r14_in), .out15(r15_in), .out16(r16_in), .out17(r17_in), .out18(r18_in), .out19(r19_in),
    .out20(r20_in), .out21(r21_in), .out22(r22_in), .out23(r23_in), .out24(r24_in), .out25(r25_in),
    .out26(r26_in), .out27(r27_in), .out28(r28_in), .out29(r29_in), .out30(r30_in), .out31(r31_in),
    .in(in_7), .sel(in_6));
  Decoder #(.select(5), .enable("false")) decoder_1 (
    .out0(r0c), .out1(r1c), .out2(r2c), .out3(r3c), .out4(r4c), .out5(r5c), .out6(r6c), .out7(r7c),
    .out8(r8c), .out9(r9c), .out10(r10c), .out11(r11c), .out12(r12c), .out13(r13c), .out14(r14c),
    .out15(r15c), .out16(r16c), .out17(r17c), .out18(r18c), .out19(r19c), .out20(r20c), .out21(r21c),
    .out22(r22c), .out23(r23c), .out24(r24c), .out25(r25c), .out26(r26c), .out27(r27c), .out28(r28c),
    .out29(r29c), .out30(r30c), .out31(r31c), .sel(in_6));
  and and_1 (and_1_out, in_1, r0c);
  and and_2 (and_2_out, in_1, r1c);
  and and_3 (and_3_out, in_1, r2c);
  and and_4 (and_4_out, in_1, r3c);
  and and_5 (and_5_out, in_1, r4c);
  and and_6 (and_6_out, in_1, r5c);
  and and_7 (and_7_out, in_1, r6c);
  and and_8 (and_8_out, in_1, r7c);
  and and_9 (and_9_out, in_1, r8c);
  and and_10 (and_10_out, in_1, r9c);
  and and_11 (and_11_out, in_1, r10c);
  and and_12 (and_12_out, in_1, r11c);
  and and_13 (and_13_out, in_1, r12c);
  and and_14 (and_14_out, in_1, r13c);
  and and_15 (and_15_out, in_1, r14c);
  and and_16 (and_16_out, in_1, r15c);
  and and_17 (and_17_out, in_1, r16c);
  and and_18 (and_18_out, in_1, r17c);
  and and_19 (and_19_out, in_1, r18c);
  and and_20 (and_20_out, in_1, r19c);
  and and_21 (and_21_out, in_1, r20c);
  and and_22 (and_22_out, in_1, r21c);
  and and_23 (and_23_out, in_1, r22c);
  and and_24 (and_24_out, in_1, r23c);
  and and_25 (and_25_out, in_1, r24c);
  and and_26 (and_26_out, in_1, r25c);
  and and_27 (and_27_out, in_1, r26c);
  and and_28 (and_28_out, in_1, r27c);
  and and_29 (and_29_out, in_1, r28c);
  and and_30 (and_30_out, in_1, r29c);
  and and_31 (and_31_out, in_1, r30c);
  and and_32 (and_32_out, in_1, r31c);
  Register #(.width(32)) Reg0 (.D(r0_in), .en(and_1_out), .Q(r0_out), .clk(in_2), .clr(in_3));
  Register #(.width(32)) Reg1 (.D(r1_in), .en(and_2_out), .Q(r1_out), .clk(in_2), .clr(in_3));
  Register #(.width(32)) Reg2 (.D(r2_in), .en(and_3_out), .Q(r2_out), .clk(in_2), .clr(in_3));
  Register #(.width(32)) Reg3 (.D(r3_in), .en(and_4_out), .Q(r3_out), .clk(in_2), .clr(in_3));
  Register #(.width(32)) Reg4 (.D(r4_in), .en(and_5_out), .Q(r4_out), .clk(in_2), .clr(in_3));
  Register #(.width(32)) Reg5 (.D(r5_in), .en(and_6_out), .Q(r5_out), .clk(in_2), .clr(in_3));
  Register #(.width(32)) Reg6 (.D(r6_in), .en(and_7_out), .Q(r6_out), .clk(in_2), .clr(in_3));
  Register #(.width(32)) Reg7 (.D(r7_in), .en(and_8_out), .Q(r7_out), .clk(in_2), .clr(in_3));
  Register #(.width(32)) Reg2_2 (.D(r8_in), .en(and_9_out), .Q(r8_out), .clk(in_2), .clr(in_3));
  Register #(.width(32)) Reg3_2 (.D(r9_in), .en(and_10_out), .Q(r9_out), .clk(in_2), .clr(in_3));
  Register #(.width(32)) Reg4_2 (.D(r10_in), .en(and_11_out), .Q(r10_out), .clk(in_2), .clr(in_3));
  Register #(.width(32)) Reg5_2 (.D(r11_in), .en(and_12_out), .Q(r11_out), .clk(in_2), .clr(in_3));
  Register #(.width(32)) Reg6_2 (.D(r12_in), .en(and_13_out), .Q(r12_out), .clk(in_2), .clr(in_3));
  Register #(.width(32)) Reg7_2 (.D(r13_in), .en(and_14_out), .Q(r13_out), .clk(in_2), .clr(in_3));
  Register #(.width(32)) Reg2_3 (.D(r14_in), .en(and_15_out), .Q(r14_out), .clk(in_2), .clr(in_3));
  Register #(.width(32)) Reg2_4 (.D(r15_in), .en(and_16_out), .Q(r15_out), .clk(in_2), .clr(in_3));
  Register #(.width(32)) Reg3_3 (.D(r16_in), .en(and_17_out), .Q(r16_out), .clk(in_2), .clr(in_3));
  Register #(.width(32)) Reg4_3 (.D(r17_in), .en(and_18_out), .Q(r17_out), .clk(in_2), .clr(in_3));
  Register #(.width(32)) Reg5_3 (.D(r18_in), .en(and_19_out), .Q(r18_out), .clk(in_2), .clr(in_3));
  Register #(.width(32)) Reg6_3 (.D(r19_in), .en(and_20_out), .Q(r19_out), .clk(in_2), .clr(in_3));
  Register #(.width(32)) Reg7_3 (.D(r20_in), .en(and_21_out), .Q(r20_out), .clk(in_2), .clr(in_3));
  Register #(.width(32)) Reg2_5 (.D(r21_in), .en(and_22_out), .Q(r21_out), .clk(in_2), .clr(in_3));
  Register #(.width(32)) Reg2_6 (.D(r22_in), .en(and_23_out), .Q(r22_out), .clk(in_2), .clr(in_3));
  Register #(.width(32)) Reg3_4 (.D(r23_in), .en(and_24_out), .Q(r23_out), .clk(in_2), .clr(in_3));
  Register #(.width(32)) Reg4_4 (.D(r24_in), .en(and_25_out), .Q(r24_out), .clk(in_2), .clr(in_3));
  Register #(.width(32)) Reg5_4 (.D(r25_in), .en(and_26_out), .Q(r25_out), .clk(in_2), .clr(in_3));
  Register #(.width(32)) Reg6_4 (.D(r26_in), .en(and_27_out), .Q(r26_out), .clk(in_2), .clr(in_3));
  Register #(.width(32)) Reg7_4 (.D(r27_in), .en(and_28_out), .Q(r27_out), .clk(in_2), .clr(in_3));
  Register #(.width(32)) Reg2_7 (.D(r28_in), .en(and_29_out), .Q(r28_out), .clk(in_2), .clr(in_3));
  Register #(.width(32)) Reg2_8 (.D(r29_in), .en(and_30_out), .Q(r29_out), .clk(in_2), .clr(in_3));
  Register #(.width(32)) Reg2_9 (.D(r30_in), .en(and_31_out), .Q(r30_out), .clk(in_2), .clr(in_3));
  Register #(.width(32)) Reg3_5 (.D(r31_in), .en(and_32_out), .Q(r31_out), .clk(in_2), .clr(in_3));
  Multiplexer #(.select(5), .width(32), .enable("false")) multiplexer_1 (
    .in0(r0_out), .in1(r1_out), .in2(r2_out), .in3(r3_out), .in4(r4_out), .in5(r5_out), .in6(r6_out),
    .in7(r7_out), .in8(r8_out), .in9(r9_out), .in10(r10_out), .in11(r11_out), .in12(r12_out), .in13(r13_out),
    .in14(r14_out), .in15(r15_out), .in16(r16_out), .in17(r17_out), .in18(r18_out), .in19(r19_out),
    .in20(r20_out), .in21(r21_out), .in22(r22_out), .in23(r23_out), .in24(r24_out), .in25(r25_out),
    .in26(r26_out), .in27(r27_out), .in28(r28_out), .in29(r29_out), .in30(r30_out), .in31(r31_out),
    .out(out_8), .sel(in_4));
  Multiplexer #(.select(5), .width(32), .enable("false")) multiplexer_2 (
    .in0(r0_out), .in1(r1_out), .in2(r2_out), .in3(r3_out), .in4(r4_out), .in5(r5_out), .in6(r6_out),
    .in7(r7_out), .in8(r8_out), .in9(r9_out), .in10(r10_out), .in11(r11_out), .in12(r12_out), .in13(r13_out),
    .in14(r14_out), .in15(r15_out), .in16(r16_out), .in17(r17_out), .in18(r18_out), .in19(r19_out),
    .in20(r20_out), .in21(r21_out), .in22(r22_out), .in23(r23_out), .in24(r24_out), .in25(r25_out),
    .in26(r26_out), .in27(r27_out), .in28(r28_out), .in29(r29_out), .in30(r30_out), .in31(r31_out),
    .out(out_9), .sel(in_5));

  // Other names for the same wires on the sheet: asyncreset = in_3; clk = in_2; data[31:0] = in_7; raddr1[4:0] = in_4;
  //   raddr1data[31:0] = out_8; raddr2[4:0] = in_5; raddr2data[31:0] = out_9; regwrite = in_1; waddr[4:0] = in_6

  // Notes on the sheet:
  //   32X32 MIPS REGISTER FILE
  //   Scematic of a 32-bit by 32 register file: each register holds a 32-bit word and there are 32 of them.
endmodule
